// Digital circuit main_processor.dig as structural Verilog
module main_processor (
  input  clk
);

  wire and_1_out, and_2_out, and_3_out, comparator_1_gt, comparator_2_eq, f, nor_1_out, S8, S9, we;
  wire [3:0] Ra, RD_MO_IMM, RS_MOV, RW;
  wire [7:0] counterpreset_1_out;
  wire [9:0] add_1_s, D_ALU, D_IMM, Din, multiplexer_1_out, multiplexer_2_out, RD1, RD2, register_2_q,
       sub_1_s;

  nor nor_1 (nor_1_out, S8, S9);
  Multiplexer #(.Selector_Bits(2), .Bits(10)) multiplexer_1 (
    .sel({S9, S8}), .in_0({10{1'b0}}), .in_1({10{1'b0}}), .in_2({10{1'b0}}), .in_3(RD1),
    .out(multiplexer_1_out));
  Multiplexer #(.Selector_Bits(2), .Bits(10)) multiplexer_2 (
    .sel({S9, S8}), .in_0({10{1'b0}}), .in_1({10{1'b0}}), .in_2({10{1'b0}}), .in_3(RD2),
    .out(multiplexer_2_out));
  Comparator #(.Bits(10)) comparator_1 (
    .a(multiplexer_1_out), .b(multiplexer_2_out), .gt(comparator_1_gt));  // open: eq, lt
  Multiplexer #(.Selector_Bits(2), .Bits(10)) multiplexer_3 (
    .sel({S9, S8}), .in_0({10{1'b0}}), .in_1(D_IMM), .in_2(RD1), .in_3(D_ALU), .out(Din));
  and and_1 (and_1_out, f, nor_1_out);
  CounterPreset #(.Bits(8)) counterpreset_1 (
    .en(1'b1), .C(clk), .dir(1'b0), .in({RS_MOV, RD_MO_IMM}), .ld(and_1_out), .clr(1'b0),
    .out(counterpreset_1_out));  // open: ovf
  and and_2 (and_2_out, S8, S9);
  Multiplexer #(.Bits(4)) multiplexer_4 (.sel(S8), .in_0(RS_MOV), .in_1(4'b0000), .out(Ra));
  Register register_1 (.D(comparator_1_gt), .C(clk), .en(and_2_out), .Q(f));
  Multiplexer #(.Selector_Bits(2)) multiplexer_5 (
    .sel({S9, S8}), .in_0(1'b0), .in_1(1'b1), .in_2(1'b1), .in_3(1'b1), .out(we));
  ROM #(.AddrBits(8), .Bits(10)) rom_1 (.A(counterpreset_1_out), .sel(1'b1), .D({S9, S8, RS_MOV, RD_MO_IMM}));
  RegisterFile #(.AddrBits(4), .Bits(10)) RF (
    .Din(Din), .we(we), .Rw(RW), .C(clk), .Ra(Ra), .Rb(4'b0001), .Da(RD1), .Db(RD2));
  Multiplexer #(.Selector_Bits(2), .Bits(4)) multiplexer_6 (
    .sel({S9, S8}), .in_0(4'b0000), .in_1(4'b0100), .in_2(RD_MO_IMM), .in_3(RD_MO_IMM), .out(RW));
  Add #(.Bits(10)) add_1 (.a(RD1), .b(RD2), .c_i(1'b0), .s(add_1_s));  // open: c_o
  Sub #(.Bits(10)) sub_1 (.a(RD1), .b(RD2), .c_i(1'b0), .s(sub_1_s));  // open: c_o
  Comparator #(.Bits(4)) comparator_2 (.a(RW), .b(4'b1000), .eq(comparator_2_eq));  // open: gt, lt
  Multiplexer #(.Selector_Bits(4), .Bits(10)) multiplexer_7 (
    .sel(RS_MOV), .in_0(add_1_s), .in_1(sub_1_s), .in_2(10'h1), .in_3(10'h1), .in_4(10'h1), .in_5(10'h1),
    .in_6(10'h1), .in_7(10'h1), .in_8(10'h1), .in_9(10'h1), .in_10(10'h1), .in_11(10'h1), .in_12(10'h1),
    .in_13(10'h1), .in_14(10'h1), .in_15(10'h1), .out(D_ALU));
  and and_3 (and_3_out, we, comparator_2_eq);
  BitExtender #(.outputBits(10)) bitextender_1 (.in({RS_MOV, RD_MO_IMM}), .out(D_IMM));
  Register #(.Bits(10)) register_2 (.D(RD1), .C(clk), .en(and_3_out), .Q(register_2_q));
  Seven_Seg_Hex seven_seg_hex_1 (.d(register_2_q[3:0]), .dp(1'b0));

  // Other names for the same wires on the sheet: S0 = RD_MO_IMM[0]; S1 = RD_MO_IMM[1]; S2 = RD_MO_IMM[2];
  //   S3 = RD_MO_IMM[3]; S4 = RS_MOV[0]; S5 = RS_MOV[1]; S6 = RS_MOV[2]; S7 = RS_MOV[3]

  // Notes on the sheet:
  //   contents of rom_1 (hex, n*v repeats v):
  //   150,249,114,243,15a,245,104,246,106,247,100,248,290,261,312,229
  //   ,290,231,312,c,101,248,290,271,302,229,250,291,312,16,100,248,3ff
endmodule
